// Digital circuit Ultimate_Bomb.dig as structural Verilog
module Ultimate_Bomb (
  input  clk,
  input  Diff,
  input  rst,
  input  k7,
  input  k6,
  input  k5,
  input  k4,
  input  k3,
  input  k2,
  input  k1,
  input  k0,
  input  countdown,
  input  [1:0] Fill_0,
  input  [7:0] Cheat,
  output WIN,
  output LOSE
);

  wire comparator_1_eq, Confirm_out, Mode_out, multiplexer_1_out, not_1_out, not_2_out, u_BCD_2_decoder_err,
       u_BIN_decoder_err, u_Level_Manager_win_flag, u_reg_setup_diff_out, u_Time_Out_Checker_time_out,
       u_Ultimate_Bomb_controller_load_max, u_Ultimate_Bomb_controller_load_min,
       u_Ultimate_Bomb_controller_load_setup, u_Ultimate_Bomb_controller_new_bomb,
       u_Ultimate_Bomb_controller_next_level;
  wire [1:0] u_Mode_Selector_mode_out, u_reg_setup_mode_out, u_Ultimate_Bomb_controller_add_time;
  wire [2:0] u_Password_Comparator_pass_gt, u_Ultimate_Bomb_controller_state_out;
  wire [3:0] multiplexer_4_out, multiplexer_4_out_2, u_Level_Manager_progress, u_Max_Register_q,
       u_Max_Register_q_2, u_Min_Register_q, u_Min_Register_q_2, u_two_bit_counter_one_out,
       u_two_bit_counter_ten_out;
  wire [7:0] multiplexer_2_out, multiplexer_3_out, u_BCD_2_decoder_seg, u_BCD_2_decoder_value,
       u_BIN_decoder_2_seg, u_BIN_decoder_seg, u_BIN_decoder_value, u_Level_Manager_score_bcd,
       u_random_rand_out;
  wire [15:0] u_State_Display_16seg_disp_1, u_State_Display_16seg_disp_2, u_State_Display_16seg_disp_3,
       u_State_Display_16seg_disp_4, u_State_Display_16seg_disp_5;
  wire [47:0] u_ROM_LED_Arranger_data;

  Button Mode (.out(Mode_out));
  BCD_2_decoder #(.applicationType("GHDL")) u_BCD_2_decoder (
    .EN(1'b1), .BCD({k7, k6, k5, k4, k3, k2, k1, k0}), .Value(u_BCD_2_decoder_value),
    .Seg(u_BCD_2_decoder_seg), .Err(u_BCD_2_decoder_err));
  BIN_decoder #(.applicationType("GHDL")) u_BIN_decoder (
    .EN(1'b1), .BIN({k7, k6, k5, k4, k3, k2, k1, k0}), .Value(u_BIN_decoder_value), .Seg(u_BIN_decoder_seg),
    .Err(u_BIN_decoder_err));
  Mode_Selector #(.applicationType("GHDL")) u_Mode_Selector (
    .clk(clk), .rst(rst), .btn_mode(Mode_out), .Mode_Out(u_Mode_Selector_mode_out));
  random #(.applicationType("GHDL")) u_random (
    .clk(clk), .rst(rst), .btn_start(u_Ultimate_Bomb_controller_new_bomb), .rand_out(u_random_rand_out));
  ROM_LED_Arranger #(.applicationType("GHDL")) u_ROM_LED_Arranger (
    .EN(1'b1), .Mode(u_reg_setup_mode_out), .Progress(u_Level_Manager_progress),
    .Data(u_ROM_LED_Arranger_data));
  Multiplexer multiplexer_1 (
    .sel(u_reg_setup_diff_out), .in_0(u_BCD_2_decoder_err), .in_1(u_BIN_decoder_err), .out(multiplexer_1_out));
  Comparator #(.Bits(8)) comparator_1 (
    .a(Cheat), .b({k7, k6, k5, k4, k3, k2, k1, k0}), .eq(comparator_1_eq));  // open: gt, lt
  BIN_decoder #(.applicationType("GHDL")) u_BIN_decoder_2 (
    .EN(1'b1), .BIN(u_random_rand_out), .Seg(u_BIN_decoder_2_seg));  // open: Value
  reg_setup #(.applicationType("GHDL")) u_reg_setup (
    .clk(clk), .rst(rst), .diff_in(Diff), .mode_in(u_Mode_Selector_mode_out),
    .en(u_Ultimate_Bomb_controller_load_setup), .mode_out(u_reg_setup_mode_out),
    .diff_out(u_reg_setup_diff_out));
  Multiplexer #(.Bits(8)) multiplexer_2 (
    .sel(u_reg_setup_diff_out), .in_0(u_BCD_2_decoder_value), .in_1(u_BIN_decoder_value),
    .out(multiplexer_2_out));
  LED led_1 (.in(u_ROM_LED_Arranger_data[23]));
  LED led_2 (.in(u_ROM_LED_Arranger_data[47]));
  Seven_Seg_Hex seven_seg_hex_1 (.d({Fill_0, u_reg_setup_mode_out}), .dp(1'b0));
  Multiplexer #(.Bits(8)) multiplexer_3 (
    .sel(u_reg_setup_diff_out), .in_0(u_BCD_2_decoder_seg), .in_1(u_BIN_decoder_seg), .out(multiplexer_3_out));
  LED led_3 (.in(u_ROM_LED_Arranger_data[22]));
  LED led_4 (.in(u_ROM_LED_Arranger_data[21]));
  LED led_5 (.in(u_ROM_LED_Arranger_data[46]));
  LED led_6 (.in(u_ROM_LED_Arranger_data[45]));
  not not_1 (not_1_out, u_reg_setup_diff_out);
  Password_Comparator #(.applicationType("GHDL")) u_Password_Comparator (
    .EnterWord(multiplexer_2_out), .Password(u_random_rand_out), .Invalid(multiplexer_1_out),
    .Pass_Gt(u_Password_Comparator_pass_gt[0]), .Pass_Match(u_Password_Comparator_pass_gt[1]),
    .Pass_Lt(u_Password_Comparator_pass_gt[2]));
  Level_Manager #(.applicationType("GHDL")) u_Level_Manager (
    .clk(clk), .rst(rst), .Mode(u_reg_setup_mode_out), .Next_Level(u_Ultimate_Bomb_controller_next_level),
    .Score_BCD(u_Level_Manager_score_bcd), .Win_Flag(u_Level_Manager_win_flag),
    .Progress(u_Level_Manager_progress));
  LED led_7 (.in(u_ROM_LED_Arranger_data[20]));
  LED led_8 (.in(u_ROM_LED_Arranger_data[19]));
  LED led_9 (.in(u_ROM_LED_Arranger_data[44]));
  LED led_10 (.in(u_ROM_LED_Arranger_data[43]));
  Seven_Seg seven_seg_1 (
    .a(not_1_out), .b(u_reg_setup_diff_out), .c(u_reg_setup_diff_out), .d(not_2_out), .e(1'b1), .f(1'b1),
    .g(1'b1), .dp(1'b0));
  LED led_11 (.in(u_ROM_LED_Arranger_data[17]));
  LED led_12 (.in(u_ROM_LED_Arranger_data[18]));
  LED led_13 (.in(u_ROM_LED_Arranger_data[41]));
  LED led_14 (.in(u_ROM_LED_Arranger_data[42]));
  not not_2 (not_2_out, u_reg_setup_diff_out);
  Seven_Seg_Hex seven_seg_hex_2 (.d(multiplexer_3_out[7:4]), .dp(1'b0));
  Multiplexer #(.Bits(8)) multiplexer_4 (
    .sel(comparator_1_eq), .in_0(u_Level_Manager_score_bcd), .in_1(u_BIN_decoder_2_seg),
    .out({multiplexer_4_out_2, multiplexer_4_out}));
  LED led_15 (.in(u_ROM_LED_Arranger_data[16]));
  LED led_16 (.in(u_ROM_LED_Arranger_data[15]));
  LED led_17 (.in(u_ROM_LED_Arranger_data[40]));
  LED led_18 (.in(u_ROM_LED_Arranger_data[39]));
  SixteenSeg sixteenseg_1 (.led(u_State_Display_16seg_disp_1), .dp(1'b0));
  Seven_Seg_Hex seven_seg_hex_3 (.d(multiplexer_3_out[3:0]), .dp(1'b0));
  LED led_19 (.in(u_ROM_LED_Arranger_data[14]));
  LED led_20 (.in(u_ROM_LED_Arranger_data[13]));
  LED led_21 (.in(u_ROM_LED_Arranger_data[38]));
  LED led_22 (.in(u_ROM_LED_Arranger_data[37]));
  SixteenSeg sixteenseg_2 (.led(u_State_Display_16seg_disp_2), .dp(1'b0));
  two_bit_counter #(.applicationType("GHDL")) u_two_bit_counter (
    .clk(countdown), .rst(rst), .add(u_Ultimate_Bomb_controller_add_time[0]),
    .en(u_Ultimate_Bomb_controller_add_time[1]), .Mode(u_reg_setup_mode_out),
    .ten_out(u_two_bit_counter_ten_out), .one_out(u_two_bit_counter_one_out));
  Ultimate_Bomb_controller #(.applicationType("GHDL")) u_Ultimate_Bomb_controller (
    .clk(clk), .Reset(rst), .EN(Confirm_out), .Time_Out(u_Time_Out_Checker_time_out),
    .Pass_Gt(u_Password_Comparator_pass_gt[0]), .Pass_Match(u_Password_Comparator_pass_gt[1]),
    .Pass_Lt(u_Password_Comparator_pass_gt[2]), .Win_Flag(u_Level_Manager_win_flag),
    .Load_Max(u_Ultimate_Bomb_controller_load_max), .Load_Min(u_Ultimate_Bomb_controller_load_min),
    .New_Bomb(u_Ultimate_Bomb_controller_new_bomb), .add_time(u_Ultimate_Bomb_controller_add_time[0]),
    .WIN(WIN), .LOSE(LOSE), .Game_Run(u_Ultimate_Bomb_controller_add_time[1]),
    .State_Out(u_Ultimate_Bomb_controller_state_out), .Next_Level(u_Ultimate_Bomb_controller_next_level),
    .Load_Setup(u_Ultimate_Bomb_controller_load_setup));
  LED led_23 (.in(u_ROM_LED_Arranger_data[11]));
  LED led_24 (.in(u_ROM_LED_Arranger_data[12]));
  LED led_25 (.in(u_ROM_LED_Arranger_data[35]));
  LED led_26 (.in(u_ROM_LED_Arranger_data[36]));
  SixteenSeg sixteenseg_3 (.led(u_State_Display_16seg_disp_3), .dp(1'b0));
  Seven_Seg_Hex seven_seg_hex_4 (.d(u_two_bit_counter_ten_out), .dp(1'b0));
  LED led_27 (.in(u_ROM_LED_Arranger_data[9]));
  LED led_28 (.in(u_ROM_LED_Arranger_data[10]));
  LED led_29 (.in(u_ROM_LED_Arranger_data[33]));
  LED led_30 (.in(u_ROM_LED_Arranger_data[34]));
  SixteenSeg sixteenseg_4 (.led(u_State_Display_16seg_disp_4), .dp(1'b0));
  LED led_31 (.in(u_ROM_LED_Arranger_data[7]));
  LED led_32 (.in(u_ROM_LED_Arranger_data[8]));
  LED led_33 (.in(u_ROM_LED_Arranger_data[31]));
  LED led_34 (.in(u_ROM_LED_Arranger_data[32]));
  Button Confirm (.out(Confirm_out));
  SixteenSeg sixteenseg_5 (.led(u_State_Display_16seg_disp_5), .dp(1'b0));
  Seven_Seg_Hex seven_seg_hex_5 (.d(u_two_bit_counter_one_out), .dp(1'b0));
  Time_Out_Checker #(.applicationType("GHDL")) u_Time_Out_Checker (
    .ones(u_two_bit_counter_one_out), .tens(u_two_bit_counter_ten_out), .Time_Out(u_Time_Out_Checker_time_out));
  LED led_35 (.in(u_ROM_LED_Arranger_data[5]));
  LED led_36 (.in(u_ROM_LED_Arranger_data[6]));
  LED led_37 (.in(u_ROM_LED_Arranger_data[29]));
  LED led_38 (.in(u_ROM_LED_Arranger_data[30]));
  Seven_Seg_Hex seven_seg_hex_6 (.d(u_Max_Register_q_2), .dp(1'b0));
  State_Display_16seg #(.applicationType("GHDL")) u_State_Display_16seg (
    .State_In(u_Ultimate_Bomb_controller_state_out), .Invalid_Input(multiplexer_1_out),
    .Disp_1(u_State_Display_16seg_disp_1), .Disp_2(u_State_Display_16seg_disp_2),
    .Disp_3(u_State_Display_16seg_disp_3), .Disp_4(u_State_Display_16seg_disp_4),
    .Disp_5(u_State_Display_16seg_disp_5));
  LED led_39 (.in(u_ROM_LED_Arranger_data[3]));
  LED led_40 (.in(u_ROM_LED_Arranger_data[4]));
  LED led_41 (.in(u_ROM_LED_Arranger_data[27]));
  LED led_42 (.in(u_ROM_LED_Arranger_data[28]));
  Seven_Seg_Hex seven_seg_hex_7 (.d(u_Max_Register_q), .dp(1'b0));
  Max_Register #(.applicationType("GHDL")) u_Max_Register (
    .clk(clk), .rst(u_Ultimate_Bomb_controller_new_bomb), .en(u_Ultimate_Bomb_controller_load_max),
    .D(multiplexer_3_out), .Q({u_Max_Register_q_2, u_Max_Register_q}));
  LED led_43 (.in(u_ROM_LED_Arranger_data[1]));
  LED led_44 (.in(u_ROM_LED_Arranger_data[2]));
  LED led_45 (.in(u_ROM_LED_Arranger_data[25]));
  LED led_46 (.in(u_ROM_LED_Arranger_data[26]));
  LED led_47 (.in(u_ROM_LED_Arranger_data[0]));
  LED led_48 (.in(u_ROM_LED_Arranger_data[24]));
  Seven_Seg_Hex seven_seg_hex_8 (.d(u_Min_Register_q_2), .dp(1'b0));
  Min_Register #(.applicationType("GHDL")) u_Min_Register (
    .clk(clk), .rst(u_Ultimate_Bomb_controller_new_bomb), .en(u_Ultimate_Bomb_controller_load_min),
    .D(multiplexer_3_out), .Q({u_Min_Register_q_2, u_Min_Register_q}));
  Seven_Seg_Hex seven_seg_hex_9 (.d(multiplexer_4_out_2), .dp(1'b0));
  Seven_Seg_Hex seven_seg_hex_10 (.d(u_Min_Register_q), .dp(1'b0));
  Seven_Seg_Hex seven_seg_hex_11 (.d(multiplexer_4_out), .dp(1'b0));

  // Notes on the sheet:
  //   clk: Hz: 5000
  //   Cheat: default 170
  //   Mode
  //   Difficulty
  //   Enter Password
  //   Entered
  //   Count Down
  //   Enter / Start
  //   Current State
  //   MAX
  //   MIN
  //   Levels
endmodule

/* Code of BCD_2_decoder:
library IEEE;
use IEEE.STD_LOGIC_1164.ALL;
use IEEE.NUMERIC_STD.ALL;

entity BCD_2_decoder is
    Port (
        EN    : in  STD_LOGIC;
        BCD   : in  STD_LOGIC_VECTOR(7 downto 0);
        Value : out STD_LOGIC_VECTOR(7 downto 0);
        Seg   : out STD_LOGIC_VECTOR(7 downto 0); -- High 4-bits: Tens, Low 4-bits: Units
        Err : out STD_LOGIC
    );
end BCD_2_decoder;

architecture Behavioral of BCD_2_decoder is
begin
    process(EN, BCD)
        variable tens_val  : integer range 0 to 15;
        variable units_val : integer range 0 to 15;
        variable bin_val   : integer range 0 to 255;
    begin
        tens_val  := to_integer(unsigned(BCD(7 downto 4)));
        units_val := to_integer(unsigned(BCD(3 downto 0)));
        
        if tens_val > 9 or units_val > 9 then
            Err <= '1';
        else
            Err <= '0';
        end if;
        
        bin_val   := (tens_val * 10) + units_val;
        
        if EN = '0' then
            Value <= (others => '0');
            Seg   <= (others => '0');
        else
            Value <= std_logic_vector(to_unsigned(bin_val, 8));
            Seg   <= BCD; -- Since BCD input is already two 4-bit numbers (tens & units)!
        end if;
    end process;
end Behavioral;
*/

/* Code of BIN_decoder:
library IEEE;
use IEEE.STD_LOGIC_1164.ALL;
use IEEE.NUMERIC_STD.ALL;

entity BIN_decoder is
    Port (
        EN    : in  STD_LOGIC;
        BIN   : in  STD_LOGIC_VECTOR(7 downto 0);
        Value : out STD_LOGIC_VECTOR(7 downto 0);
        Seg   : out STD_LOGIC_VECTOR(7 downto 0);  -- High 4-bits: Tens, Low 4-bits: Units
        Err   : out STD_LOGIC
    );
end BIN_decoder;

architecture Behavioral of BIN_decoder is
begin
    process(EN, BIN)
        variable bin_val   : integer range 0 to 255;
        variable tens_int  : integer range 0 to 31;
        variable units_int : integer range 0 to 15;
    begin
        bin_val := to_integer(unsigned(BIN));
        
        if bin_val > 99 then
            Err <= '1';
        else
            Err <= '0';
        end if;
        
        if EN = '0' then
            Value <= (others => '0');
            Seg   <= (others => '0');
        else
            Value <= BIN;
            
            tens_int  := bin_val / 10;
            units_int := bin_val mod 10;
            
            Seg <= std_logic_vector(to_unsigned(tens_int, 4)) & std_logic_vector(to_unsigned(units_int, 4));
        end if;
    end process;

end Behavioral;
*/

/* Code of Mode_Selector:
library IEEE;
use IEEE.STD_LOGIC_1164.ALL;
use IEEE.NUMERIC_STD.ALL;

entity Mode_Selector is
    Port (
        clk      : in  STD_LOGIC;
        rst      : in  STD_LOGIC;
        btn_mode : in  STD_LOGIC;
        Mode_Out : out STD_LOGIC_VECTOR(1 downto 0)
    );
end Mode_Selector;

architecture Behavioral of Mode_Selector is
    signal mode_reg : unsigned(1 downto 0) := "00";
    signal btn_prev : std_logic := '0';
begin

    process(clk, rst)
    begin
        if rst = '1' then
            mode_reg <= "00";
            btn_prev <= '0';
        elsif rising_edge(clk) then
            -- 按鍵上升緣偵測 (避免按住時連續瘋狂跳動)
            if btn_mode = '1' and btn_prev = '0' then
                mode_reg <= mode_reg + 1;
            end if;
            btn_prev <= btn_mode;
        end if;
    end process;

    Mode_Out <= std_logic_vector(mode_reg);

end Behavioral;
*/

/* Code of random:
library IEEE;
use IEEE.STD_LOGIC_1164.ALL;
use IEEE.NUMERIC_STD.ALL;

entity random is
    Port ( 
        clk        : in  STD_LOGIC;
        rst        : in  STD_LOGIC;
        btn_start  : in  STD_LOGIC;
        rand_out   : out STD_LOGIC_VECTOR(7 downto 0));
end random;

architecture Behavioral of random is
    signal fast_counter : unsigned(7 downto 0) := "00000000";
    signal latched_val  : unsigned(7 downto 0) := "00000000";
begin

    process(clk, rst)
    begin
        if rst = '1' then
            fast_counter <= "00000000";
        elsif rising_edge(clk) then
            if fast_counter = 99 then
                fast_counter <= "00000000";
            else
                fast_counter <= fast_counter + 1;
            end if;
        end if;
    end process;

    process(clk, rst)
    begin
        if rst = '1' then
            latched_val <= "00000000";
        elsif rising_edge(clk) then
            if btn_start = '1' then
                latched_val <= fast_counter;
            end if;
        end if;
    end process;
    rand_out <= std_logic_vector(latched_val);

end Behavioral;
*/

/* Code of ROM_LED_Arranger:
library IEEE;
use IEEE.STD_LOGIC_1164.ALL;
use IEEE.NUMERIC_STD.ALL;

entity ROM_LED_Arranger is
    Port (
        EN       : in  STD_LOGIC;
        Mode     : in  STD_LOGIC_VECTOR(1 downto 0);
        Progress : in  STD_LOGIC_VECTOR(3 downto 0);
        Data     : out STD_LOGIC_VECTOR(47 downto 0)  -- 48 LED, upper row then lower row
    );
end ROM_LED_Arranger;

architecture Behavioral of ROM_LED_Arranger is

    -------------------------------------------------------------------------
    -- 24‑bit ROM type – one row (左到右編號：左端為高位元，右端為低位元)
    -------------------------------------------------------------------------
    type rom24_type is array (0 to 15) of std_logic_vector(23 downto 0);

    -- Row‑wise helper constants
    constant ALL_ON_24  : std_logic_vector(23 downto 0) := x"FFFFFF";  -- 24 個 1
    constant ALL_OFF_24 : std_logic_vector(23 downto 0) := x"000000";  -- 24 個 0

    -------------------------------------------------------------------------
    -- Mode 0 : idle – both rows always off
    -------------------------------------------------------------------------
    constant MODE0_UP_ROM  : rom24_type := (others => ALL_OFF_24);
    constant MODE0_LOW_ROM : rom24_type := (others => ALL_OFF_24);

    -------------------------------------------------------------------------
    -- Mode 1 : Fin = 3 – 右側每次清除 8 顆 LED (共 3 步)
    -------------------------------------------------------------------------
    constant MODE1_UP_ROM : rom24_type := (
        0 => ALL_ON_24,   -- 111111111111111111111111
        1 => x"FFFF00",   -- 右側 8 顆熄滅
        2 => x"FF0000",   -- 右側 16 顆熄滅
        3 => ALL_OFF_24,
        others => ALL_OFF_24
    );
    constant MODE1_LOW_ROM : rom24_type := (
        0 => ALL_ON_24,
        1 => x"FFFF00",
        2 => x"FF0000",
        3 => ALL_OFF_24,
        others => ALL_OFF_24
    );

    -------------------------------------------------------------------------
    -- Mode 2 : Fin = 6 – 右側每次清除 4 顆 LED (共 6 步)
    -------------------------------------------------------------------------
    constant MODE2_UP_ROM : rom24_type := (
        0 => ALL_ON_24,
        1 => x"FFFFF0",   -- clear 4 LSB
        2 => x"FFFF00",   -- clear 8 LSB
        3 => x"FFF000",   -- clear 12 LSB
        4 => x"FF0000",   -- clear 16 LSB
        5 => x"F00000",   -- clear 20 LSB
        6 => x"000000",   -- clear 24 LSB (全部熄滅)
        others => ALL_OFF_24
    );
    constant MODE2_LOW_ROM : rom24_type := (
        0 => ALL_ON_24,
        1 => x"FFFFF0",
        2 => x"FFFF00",
        3 => x"FFF000",
        4 => x"FF0000",
        5 => x"F00000",
        6 => x"000000",
        others => ALL_OFF_24
    );

    -------------------------------------------------------------------------
    -- Mode 3 : Fin = 12 – 右側每次清除 2 顆 LED (共 12 步)
    -------------------------------------------------------------------------
    constant MODE3_UP_ROM : rom24_type := (
        0  => ALL_ON_24,   -- 111111111111111111111111
        1  => x"FFFFFC",   -- clear 2 LSB
        2  => x"FFFFF0",   -- clear 4 LSB
        3  => x"FFFFC0",   -- clear 6 LSB
        4  => x"FFFF00",   -- clear 8 LSB
        5  => x"FFFC00",   -- clear 10 LSB
        6  => x"FFF000",   -- clear 12 LSB
        7  => x"FFC000",   -- clear 14 LSB
        8  => x"FF0000",   -- clear 16 LSB
        9  => x"FC0000",   -- clear 18 LSB
        10 => x"F00000",   -- clear 20 LSB
        11 => x"C00000",   -- clear 22 LSB
        others => ALL_OFF_24
    );
    constant MODE3_LOW_ROM : rom24_type := (
        0  => ALL_ON_24,
        1  => x"FFFFFC",
        2  => x"FFFFF0",
        3  => x"FFFFC0",
        4  => x"FFFF00",
        5  => x"FFFC00",
        6  => x"FFF000",
        7  => x"FFC000",
        8  => x"FF0000",
        9  => x"FC0000",
        10 => x"F00000",
        11 => x"C00000",
        others => ALL_OFF_24
    );

begin

    process(EN, Mode, Progress)
        variable idx : integer range 0 to 15;
        variable up_row  : std_logic_vector(23 downto 0);
        variable low_row : std_logic_vector(23 downto 0);
    begin
        idx := to_integer(unsigned(Progress));
        if EN = '0' then
            Data <= (others => '0');
        else
            case Mode is
                when "00" =>
                    up_row  := MODE1_UP_ROM(idx);
                    low_row := MODE1_LOW_ROM(idx);
                when "01" =>
                    up_row  := MODE2_UP_ROM(idx);
                    low_row := MODE2_LOW_ROM(idx);
                when "10" =>
                    up_row  := MODE3_UP_ROM(idx);
                    low_row := MODE3_LOW_ROM(idx);
                when "11" =>
                    up_row  := ALL_ON_24;
                    low_row := ALL_ON_24;
                when others =>
                    up_row  := ALL_OFF_24;
                    low_row := ALL_OFF_24;
            end case;
            Data <= up_row & low_row;  -- upper row (bits 47..24) + lower row (bits 23..0)
        end if;
    end process;

end Behavioral;
*/

/* Code of BIN_decoder:
library IEEE;
use IEEE.STD_LOGIC_1164.ALL;
use IEEE.NUMERIC_STD.ALL;

entity BIN_decoder is
    Port (
        EN    : in  STD_LOGIC;
        BIN   : in  STD_LOGIC_VECTOR(7 downto 0);        
        Seg   : out STD_LOGIC_VECTOR(7 downto 0);  -- High 4-bits: Tens, Low 4-bits: Units
	Value : out STD_LOGIC_VECTOR(7 downto 0)    
);
end BIN_decoder;

architecture Behavioral of BIN_decoder is
begin
    process(EN, BIN)
        variable bin_val   : integer range 0 to 255;
        variable tens_int  : integer range 0 to 31;
        variable units_int : integer range 0 to 15;
    begin
        bin_val := to_integer(unsigned(BIN));
        
        if EN = '0' then
            Value <= (others => '0');
            Seg   <= (others => '0');
        else
            Value <= BIN;
            
            tens_int  := bin_val / 10;
            units_int := bin_val mod 10;
            
            Seg <= std_logic_vector(to_unsigned(tens_int, 4)) & std_logic_vector(to_unsigned(units_int, 4));
        end if;
    end process;

end Behavioral;
*/

/* Code of reg_setup:
library IEEE;
use IEEE.STD_LOGIC_1164.ALL;

entity reg_setup is
    Port ( 
        clk : in  STD_LOGIC;
        rst : in  STD_LOGIC;
        diff_in  : in  STD_LOGIC;                   
        mode_in  : in  STD_LOGIC_VECTOR(1 downto 0);                   
        en  : in  STD_LOGIC;                   
        mode_out  : out  STD_LOGIC_VECTOR(1 downto 0);                   
        diff_out  : out  STD_LOGIC                   
    );
end reg_setup;

architecture Behavioral of reg_setup is
signal tmp_diff: STD_LOGIC:= '0';
signal tmp_mode: STD_LOGIC_VECTOR(1 downto 0):= "00";
begin
    process(clk, rst)
    begin
        tmp_diff <= diff_in;
        tmp_mode <= mode_in;
        if rst = '1' then
            tmp_mode <= "00";
            tmp_diff <= '0';
        elsif rising_edge(clk) then
            if en = '1' then
                mode_out <= tmp_mode;
                diff_out <= tmp_diff;
            end if;
        end if;
    end process;
end Behavioral;
*/

/* Code of Password_Comparator:
library IEEE;
use IEEE.STD_LOGIC_1164.ALL;
use IEEE.NUMERIC_STD.ALL;

entity Password_Comparator is
    Port (
        EnterWord : in  STD_LOGIC_VECTOR(7 downto 0);
        Password  : in  STD_LOGIC_VECTOR(7 downto 0);
        Invalid   : in  STD_LOGIC;  -- 密碼是否無效
        Pass_Gt   : out STD_LOGIC;  -- EnterWord > Password
        Pass_Match: out STD_LOGIC;  -- EnterWord = Password
        Pass_Lt   : out STD_LOGIC   -- EnterWord < Password
    );
end Password_Comparator;

architecture Behavioral of Password_Comparator is
begin
    process(EnterWord, Password, Invalid)
        variable val_A : integer;
        variable val_B : integer;
    begin
        val_A := to_integer(unsigned(EnterWord));
        val_B := to_integer(unsigned(Password));
        
        -- 預設歸零
        Pass_Gt <= '0';
        Pass_Match <= '0';
        Pass_Lt <= '0';
        
        if Invalid = '0' then
            if val_A > val_B then
                Pass_Gt <= '1';
            elsif val_A < val_B then
                Pass_Lt <= '1';
            else
                Pass_Match <= '1';
            end if;
        end if;
    end process;
end Behavioral;
*/

/* Code of Level_Manager:
library IEEE;
use IEEE.STD_LOGIC_1164.ALL;
use IEEE.NUMERIC_STD.ALL;

entity Level_Manager is
    Port (
        clk        : in  STD_LOGIC;
        rst        : in  STD_LOGIC;
        Mode       : in  STD_LOGIC_VECTOR(1 downto 0);
        Next_Level : in  STD_LOGIC; -- 來自 Controller 的破關脈衝
        
        Score_BCD  : out STD_LOGIC_VECTOR(7 downto 0);  -- 總破關數 (BCD 碼輸出，可以直接接兩顆七段顯示器)
        Win_Flag   : out STD_LOGIC;                   -- 告訴 Controller 破關了沒
        Progress   : out STD_LOGIC_VECTOR(3 downto 0) -- 給 LED 顯示進度
    );
end Level_Manager;

architecture Behavioral of Level_Manager is
    signal Finish_stages : integer range 0 to 15 := 3;
    signal Solved        : integer range 0 to 15 := 0;
    
    -- 用來計數總破關數的變數 (支援到 99 關)
    signal score_tens  : integer range 0 to 9 := 0;
    signal score_units : integer range 0 to 9 := 0;
begin
    
    Progress <= std_logic_vector(to_unsigned(Solved, 4));
    Score_BCD(7 downto 4) <= std_logic_vector(to_unsigned(score_tens, 4));
    Score_BCD(3 downto 0) <= std_logic_vector(to_unsigned(score_units, 4));

    -- Combinational Logic for Finish_stages and Win_Flag
    process(Mode, Solved, Finish_stages)
    begin
        -- 判斷目標關卡數
        if Mode = "00" then
            Finish_stages <= 3;
        elsif Mode = "01" then
            Finish_stages <= 6;
        else -- "10" or "11"
            Finish_stages <= 12;
        end if;
        
        -- 判斷是否達成通關條件 (如果再過一關就達到目標，且不是無盡模式)
        if Mode = "11" then
            Win_Flag <= '0'; -- 無盡模式永遠不觸發 Win_Flag
        elsif (Solved + 1) >= Finish_stages then
            Win_Flag <= '1';
        else
            Win_Flag <= '0';
        end if;
    end process;

    -- Sequential Logic for counting Solved stages
    process(clk, rst)
    begin
        if rst = '1' then
            Solved <= 0;
            score_tens <= 0;
            score_units <= 0;
        elsif rising_edge(clk) then
            if Next_Level = '1' then
                
                -- 更新總分 (Score)
                if score_units = 9 then
                    score_units <= 0;
                    if score_tens /= 9 then
                        score_tens <= score_tens + 1;
                    end if;
                else
                    score_units <= score_units + 1;
                end if;
                if Mode = "11" then
                    -- 無盡模式：不更動關卡進度條 (LED 不動)
                    Solved <= 0;
                elsif Solved < Finish_stages then
                    -- 普通模式：還沒滿就繼續加
                    Solved <= Solved + 1;
                end if;
            end if;
        end if;
    end process;

end Behavioral;
*/

/* Code of two_bit_counter:
LIBRARY IEEE;
USE IEEE.STD_LOGIC_1164.ALL;
USE IEEE.NUMERIC_STD.ALL;

ENTITY two_bit_counter is
    PORT (  clk     : in     STD_LOGIC;
            rst     : in     STD_LOGIC;
            add     : in     STD_LOGIC;
            en      : in     STD_LOGIC;  -- Game_Run
            Mode    : in     STD_LOGIC_VECTOR(1 downto 0);
            ten_out : out    STD_LOGIC_VECTOR (3 downto 0);
            one_out : out    STD_LOGIC_VECTOR (3 downto 0)
         );
END two_bit_counter;

ARCHITECTURE Behavioral of two_bit_counter is
    signal tens : unsigned(3 downto 0) := "1001";
    signal ones : unsigned(3 downto 0) := "1001";
    signal add_flag : std_logic := '0';
begin

    -- 捕捉來自高速時脈的 add 脈衝 (Pulse Catcher)
    process(clk, rst, add)
    begin
        if rst = '1' then
            add_flag <= '0';
        elsif add = '1' then
            add_flag <= '1';
        elsif rising_edge(clk) then
            add_flag <= '0';
        end if;
    end process;

    process(clk, rst)
        variable bonus_tens : unsigned(3 downto 0);
    begin
        if rst = '1' then
            tens <= "1001";
            ones <= "1001";
        elsif rising_edge(clk) then
            if add_flag = '1' then                
              if Mode = "00" then
                  bonus_tens := "0011"; -- 入門: +30秒
              elsif Mode = "10" then
                  bonus_tens := "0001"; -- 挑戰: +10秒
              else
                  bonus_tens := "0010"; -- 進階與無盡: +20秒
              end if;
              
              if (tens + bonus_tens) >= 9 then                  
                 tens <= "1001";
                 ones <= "1001";
              else
                 tens <= tens + bonus_tens;
              end if;
            elsif en = '1' then   -- 如果你目前全場只用一個 1Hz 時鐘，就直接這樣寫
                if tens = 0 and ones = 0 then
                    -- 已經是 00，保持不變
                    tens <= "0000";
                    ones <= "0000";
                elsif ones = 0 then
                    -- 個位數為 0，向十位數借位
                    ones <= "1001";
                    tens <= tens - 1;
                else
                    -- 正常個位數減 1
                    ones <= ones - 1;
                end if;
            end if;
        end if;
    end process;
    ten_out <= std_logic_vector(tens);
    one_out <= std_logic_vector(ones);

end Behavioral;
*/

/* Code of Ultimate_Bomb_controller:
library IEEE;
use IEEE.STD_LOGIC_1164.ALL;
use IEEE.NUMERIC_STD.ALL;

entity Ultimate_Bomb_controller is
    Port (
        clk        : in  STD_LOGIC;  
        Reset      : in  STD_LOGIC;
        EN         : in  STD_LOGIC;  -- Enter 鍵
        
        -- 外部狀態輸入 (代替原本的 8-bit 數字，由外部的 Comparator 產生)
        Time_Out   : in  STD_LOGIC;  -- 倒數計時為 0 的訊號
        Pass_Gt    : in  STD_LOGIC;  -- 輸入 > 密碼
        Pass_Match : in  STD_LOGIC;  -- 輸入 == 密碼
        Pass_Lt    : in  STD_LOGIC;  -- 輸入 < 密碼
        
        -- 給 Level Manager 的介面
        Win_Flag   : in  STD_LOGIC;  -- 來自 Level Manager：是否達成通關條件
        
        -- 對外部 Datapath 的控制輸出
        Load_Max   : out STD_LOGIC;  -- 叫外部 Max 暫存器更新
        Load_Min   : out STD_LOGIC;  -- 叫外部 Min 暫存器更新
        New_Bomb   : out STD_LOGIC;  -- 叫亂數產生器產生新密碼 (兼具 Reset 上下限的功能)
        add_time   : out STD_LOGIC;  -- 叫計時器加時間
        WIN        : out STD_LOGIC;
        LOSE       : out STD_LOGIC;
        Game_Run   : out STD_LOGIC;  -- 告訴倒數計時器現在可以倒數了
        State_Out  : out STD_LOGIC_VECTOR(2 downto 0); -- 輸出當前狀態給顯示器
        
        -- 給 Level Manager 的介面
        Next_Level : out STD_LOGIC;  -- 給 Level Manager：破關了，進度加一
        
        -- ★ 新增：用來鎖死外部 Difficulty 與 Mode 暫存器的控制訊號
        Load_Setup : out STD_LOGIC   
    );
end Ultimate_Bomb_controller;

architecture Behavioral of Ultimate_Bomb_controller is
    type state_type is (idle, next_bomb, game, check_pass, game_win, game_lose);
    signal current_state : state_type := idle;
    
    signal EN_prev : STD_LOGIC := '0';
begin

    -- 狀態顯示解碼器 (單純組合邏輯)
    process(current_state)
    begin
        case current_state is
            when idle       => State_Out <= "000";
            when next_bomb  => State_Out <= "001";
            when game       => State_Out <= "010";
            when check_pass => State_Out <= "010";
            when game_win   => State_Out <= "011";
            when game_lose  => State_Out <= "100";
            when others     => State_Out <= "000";
        end case;
    end process;

    -- 核心狀態機 (同步循序邏輯)
    process(clk, Reset)
    begin
        if Reset = '1' then
            current_state <= idle;
            WIN <= '0';
            LOSE <= '0';
            Game_Run <= '0';
            New_Bomb <= '0';
            add_time <= '0';
            Load_Max <= '0';
            Load_Min <= '0';
            Load_Setup <= '0'; -- ★ 新增：重置時關閉設定大門
            EN_prev <= '0';
            
        elsif rising_edge(clk) then
            -- 預設所有脈衝控制訊號為 0 (避免產生 Latch)
            New_Bomb <= '0';
            add_time <= '0';
            Next_Level <= '0';
            Load_Max <= '0';
            Load_Min <= '0';
            Load_Setup <= '0'; -- ★ 新增：預設關閉大門，保持暫存器鎖定狀態
            
            EN_prev <= EN; 
            
            -- 時間到直接輸 (例外處理：如果在閒置或已經結束的狀態就不理會)
            if current_state /= idle and current_state /= game_win and current_state /= game_lose then
                if Time_Out = '1' then
                    current_state <= game_lose;
                end if;
            end if;

            case current_state is
                when idle =>
                    WIN <= '0';
                    LOSE <= '0';
                    Game_Run <= '0';
                    Load_Setup <= '1';
                    
                    if EN = '1' and EN_prev = '0' then
                        current_state <= next_bomb; 
                    end if;
                    
                when next_bomb =>
                    New_Bomb <= '1'; 
                    Game_Run <= '0';
                    
                    if EN = '1' and EN_prev = '0' then
                        current_state <= game;
                    end if;
                    
                when game =>
                    Game_Run <= '1';
                    if EN = '1' and EN_prev = '0' then
                        current_state <= check_pass;
                    end if;
                    
                when check_pass =>
                    Game_Run <= '1';
                    if Pass_Gt = '1' then
                        Load_Max <= '1'; 
                        current_state <= game;
                    elsif Pass_Lt = '1' then
                        Load_Min <= '1'; 
                        current_state <= game;
                    elsif Pass_Match = '1' then
                        add_time <= '1';
                        Next_Level <= '1'; 
                        
                        if Win_Flag = '1' then
                            current_state <= game_win;
                        else
                            current_state <= next_bomb;
                        end if;
                    else
                        current_state <= game; 
                    end if;
                    
                when game_win =>
                    WIN <= '1';
                    Game_Run <= '0';
                    
                when game_lose =>
                    LOSE <= '1';
                    Game_Run <= '0';
                    
            end case;
        end if;
    end process;
end Behavioral;
*/

/* Code of Time_Out_Checker:
library IEEE;
use IEEE.STD_LOGIC_1164.ALL;

entity Time_Out_Checker is
    Port (
        ones     : in  STD_LOGIC_VECTOR(3 downto 0);
        tens     : in  STD_LOGIC_VECTOR(3 downto 0);
        Time_Out : out STD_LOGIC
    );
end Time_Out_Checker;

architecture Behavioral of Time_Out_Checker is
begin
    -- 當十位數和個位數都為 0 時，輸出 Time_Out = '1'
    process(tens, ones)
    begin
        if tens = "0000" and ones = "0000" then
            Time_Out <= '1';
        else
            Time_Out <= '0';
        end if;
    end process;
end Behavioral;
*/

/* Code of State_Display_16seg:
library IEEE;
use IEEE.STD_LOGIC_1164.ALL;

entity State_Display_16seg is
    Port (
        State_In      : in  STD_LOGIC_VECTOR(2 downto 0);
        Invalid_Input : in  STD_LOGIC;
        Disp_1        : out STD_LOGIC_VECTOR(15 downto 0);
        Disp_2        : out STD_LOGIC_VECTOR(15 downto 0);
        Disp_3        : out STD_LOGIC_VECTOR(15 downto 0);
        Disp_4        : out STD_LOGIC_VECTOR(15 downto 0);
        Disp_5        : out STD_LOGIC_VECTOR(15 downto 0)
    );
end State_Display_16seg;

architecture Behavioral of State_Display_16seg is
    -- 16-Segment Bit Mapping (Based on typical Digital simulator layout)
    -- Bit 0: a1 (top left)
    -- Bit 1: a2 (top right)
    -- Bit 2: b  (top right vertical)
    -- Bit 3: c  (bottom right vertical)
    -- Bit 4: d2 (bottom right)
    -- Bit 5: d1 (bottom left)
    -- Bit 6: e  (bottom left vertical)
    -- Bit 7: f  (top left vertical)
    -- Bit 8: g1 (middle left horizontal)
    -- Bit 9: g2 (middle right horizontal)
    -- Bit 10: h (top left diagonal)
    -- Bit 11: i (top middle vertical)
    -- Bit 12: j (top right diagonal)
    -- Bit 13: k (bottom right diagonal)
    -- Bit 14: l (bottom middle vertical)
    -- Bit 15: m (bottom left diagonal)
    
    constant BLANK : std_logic_vector(15 downto 0) := x"0000";
    constant CHAR_E: std_logic_vector(15 downto 0) := x"03F3"; -- a1,a2, d1,d2, e,f, g1,g2 -> 0,1, 4,5, 6,7, 8,9
    constant CHAR_R: std_logic_vector(15 downto 0) := x"23C7"; -- a1,a2, b, e,f, g1,g2, k -> 0,1, 2, 6,7, 8,9, 13
    constant CHAR_O: std_logic_vector(15 downto 0) := x"00FF"; -- a1,a2, b,c, d1,d2, e,f -> 0,1, 2,3, 4,5, 6,7
    constant CHAR_L: std_logic_vector(15 downto 0) := x"00F0"; -- d1,d2, e,f -> 4,5, 6,7
    constant CHAR_S: std_logic_vector(15 downto 0) := x"03BB"; -- a1,a2, c, d1,d2, f, g1,g2 -> 0,1, 3, 4,5, 7, 8,9
    constant CHAR_W: std_logic_vector(15 downto 0) := x"A0FC"; -- b,c, d1,d2, e,f, m,k -> 2,3, 4,5, 6,7, 13,15
    constant CHAR_I: std_logic_vector(15 downto 0) := x"4800"; -- i, l -> 11, 14
    constant CHAR_N: std_logic_vector(15 downto 0) := x"24CC"; -- b,c, e,f, h,k -> 2,3, 6,7, 10,13
    constant CHAR_P: std_logic_vector(15 downto 0) := x"03C7"; -- a1,a2, b, e,f, g1,g2 -> 0,1, 2, 6,7, 8,9
    constant CHAR_U: std_logic_vector(15 downto 0) := x"00FC"; -- b,c, d1,d2, e,f -> 2,3, 4,5, 6,7
    constant CHAR_T: std_logic_vector(15 downto 0) := x"4803"; -- a1,a2, i, l -> 0,1, 11, 14
    constant CHAR_D: std_logic_vector(15 downto 0) := x"483F"; -- a1,a2, b,c, d1,d2, i,l -> 0,1, 2,3, 4,5, 11,14
    constant CHAR_X: std_logic_vector(15 downto 0) := x"B400"; -- h, j, k, m -> 10, 12, 13, 15

begin
    process(State_In, Invalid_Input)
    begin
        if Invalid_Input = '1' then
            -- ERROR
            Disp_1 <= CHAR_E;
            Disp_2 <= CHAR_R;
            Disp_3 <= CHAR_R;
            Disp_4 <= CHAR_O;
            Disp_5 <= CHAR_R;
        else
            case State_In is
                when "000" => -- idle (IDLE )
                    Disp_1 <= CHAR_I;
                    Disp_2 <= CHAR_D;
                    Disp_3 <= CHAR_L;
                    Disp_4 <= CHAR_E;
                    Disp_5 <= BLANK;
                    
                when "001" => -- next_bomb (NEXT )
                    Disp_1 <= CHAR_N;
                    Disp_2 <= CHAR_E;
                    Disp_3 <= CHAR_X;
                    Disp_4 <= CHAR_T;
                    Disp_5 <= BLANK;
                    
                when "010" => -- game / check_pass (INPUT)
                    Disp_1 <= CHAR_I;
                    Disp_2 <= CHAR_N;
                    Disp_3 <= CHAR_P;
                    Disp_4 <= CHAR_U;
                    Disp_5 <= CHAR_T;
                    
                when "011" => -- game_win ( WIN )
                    Disp_1 <= BLANK;
                    Disp_2 <= CHAR_W;
                    Disp_3 <= CHAR_I;
                    Disp_4 <= CHAR_N;
                    Disp_5 <= BLANK;
                    
                when "100" => -- game_lose (LOSE )
                    Disp_1 <= CHAR_L;
                    Disp_2 <= CHAR_O;
                    Disp_3 <= CHAR_S;
                    Disp_4 <= CHAR_E;
                    Disp_5 <= BLANK;
                    
                when others =>
                    Disp_1 <= BLANK;
                    Disp_2 <= BLANK;
                    Disp_3 <= BLANK;
                    Disp_4 <= BLANK;
                    Disp_5 <= BLANK;
            end case;
        end if;
    end process;
end Behavioral;
*/

/* Code of Max_Register:
library IEEE;
use IEEE.STD_LOGIC_1164.ALL;
use IEEE.NUMERIC_STD.ALL;

entity Max_Register is
    Port (
        clk : in  STD_LOGIC;
        rst : in  STD_LOGIC;  -- 接 New_Bomb 或 系統 Reset
        en  : in  STD_LOGIC;  -- 接 Load_Max
        D   : in  STD_LOGIC_VECTOR(7 downto 0); -- 接玩家輸入的數字
        Q   : out STD_LOGIC_VECTOR(7 downto 0)  -- 輸出給顯示器
    );
end Max_Register;

architecture Behavioral of Max_Register is
    -- 預設為 BCD 碼的 99 (1001 1001)
    signal reg_data : STD_LOGIC_VECTOR(7 downto 0) := "10011001"; 
begin
    process(clk, rst)
    begin
        -- 當 rst=1 (收到 New_Bomb 訊號) 時，強制恢復成 99
        if rst = '1' then
            reg_data <= "10011001"; 
        elsif rising_edge(clk) then
            if en = '1' then
                if unsigned(D) < unsigned(reg_data) then
                    reg_data <= D; -- 只有輸入數字比當前範圍小時，才會更新
                end if;
            end if;
        end if;
    end process;
    
    Q <= reg_data;
end Behavioral;
*/

/* Code of Min_Register:
library IEEE;
use IEEE.STD_LOGIC_1164.ALL;
use IEEE.NUMERIC_STD.ALL;

entity Min_Register is
    Port (
        clk : in  STD_LOGIC;
        rst : in  STD_LOGIC;  -- 接 New_Bomb 或 系統 Reset
        en  : in  STD_LOGIC;  -- 接 Load_Min
        D   : in  STD_LOGIC_VECTOR(7 downto 0); -- 接玩家輸入的數字
        Q   : out STD_LOGIC_VECTOR(7 downto 0)  -- 輸出給顯示器
    );
end Min_Register;

architecture Behavioral of Min_Register is
    -- 預設為 BCD 碼的 00 (0000 0000)
    signal reg_data : STD_LOGIC_VECTOR(7 downto 0) := "00000000"; 
begin
    process(clk, rst)
    begin
        -- 當 rst=1 (收到 New_Bomb 訊號) 時，強制恢復成 00
        if rst = '1' then
            reg_data <= "00000000"; 
        elsif rising_edge(clk) then
            if en = '1' then
                if unsigned(D) > unsigned(reg_data) then
                    reg_data <= D; -- 只有輸入數字比當前範圍大時，才會更新
                end if;
            end if;
        end if;
    end process;
    
    Q <= reg_data;
end Behavioral;
*/
